// Logisim project Codificador.circ as structural Verilog: 4 circuits, main circuit Codificador
module Codificador (
  input  A,
  input  B,
  input  C,
  input  D,
  output S3,
  output S2,
  output S1,
  output S0
);

  wire and_1_out, and_2_out, and_3_out, and_4_out, and_5_out, and_6_out, and_7_out, and_8_out, and_9_out,
       and_10_out, and_11_out, and_12_out, and_13_out, and_14_out, and_15_out, and_16_out, and_17_out,
       not_1_out, not_2_out, not_3_out, not_4_out, not_5_out, not_6_out, not_7_out, not_8_out, not_9_out,
       not_10_out, not_11_out, not_12_out, not_13_out, not_14_out, not_15_out, not_16_out, not_17_out,
       not_18_out, not_19_out, not_20_out, not_21_out, not_22_out, not_23_out;

  not not_1 (not_1_out, A);
  not not_2 (not_2_out, B);
  and and_1 (and_1_out, not_1_out, not_2_out, not_3_out);
  not not_3 (not_3_out, C);
  not not_4 (not_4_out, B);
  and and_2 (and_2_out, not_4_out, D);
  not not_5 (not_5_out, A);
  and and_3 (and_3_out, not_5_out, C, D);
  and and_4 (and_4_out, A, B, not_6_out);
  not not_6 (not_6_out, D);
  not not_7 (not_7_out, A);
  and and_5 (and_5_out, not_7_out, not_8_out);
  not not_8 (not_8_out, D);
  not not_9 (not_9_out, A);
  and and_6 (and_6_out, not_9_out, C);
  and and_7 (and_7_out, B, C);
  not not_10 (not_10_out, A);
  not not_11 (not_11_out, B);
  not not_12 (not_12_out, C);
  not not_13 (not_13_out, A);
  not not_14 (not_14_out, C);
  not not_15 (not_15_out, D);
  not not_16 (not_16_out, A);
  not not_17 (not_17_out, C);
  not not_18 (not_18_out, B);
  not not_19 (not_19_out, D);
  not not_20 (not_20_out, A);
  and and_8 (and_8_out, not_20_out, C, D);
  and and_9 (and_9_out, B, D);
  not not_21 (not_21_out, A);
  and and_10 (and_10_out, not_21_out, B, C);
  and and_11 (and_11_out, A, not_22_out, D);
  not not_22 (not_22_out, C);
  and and_12 (and_12_out, A, B, not_23_out);
  not not_23 (not_23_out, C);
  or or_1 (S3, and_1_out, and_2_out, and_3_out, and_4_out);
  or or_2 (S2, and_5_out, and_6_out, and_7_out);
  and and_13 (and_13_out, not_10_out, not_11_out, not_12_out);
  and and_14 (and_14_out, not_13_out, not_14_out, not_15_out);
  and and_15 (and_15_out, not_16_out, B, C);
  and and_16 (and_16_out, A, not_17_out, D);
  and and_17 (and_17_out, A, not_18_out, C, not_19_out);
  or or_3 (S0, and_8_out, and_9_out, and_10_out, and_11_out, and_12_out);
  or or_4 (S1, and_13_out, and_14_out, and_15_out, and_16_out, and_17_out);
endmodule

module Codificador__Exemplo (
  input  RD,
  input  RS,
  input  A,
  input  B,
  input  C,
  input  D,
  output S3,
  output S2,
  output S1,
  output S0
);

  wire and_1_out, and_2_out, and_3_out, and_4_out, and_5_out, and_6_out, and_7_out, and_8_out, and_9_out,
       and_10_out, and_11_out, and_12_out, and_13_out, and_14_out, and_15_out, and_16_out, and_17_out,
       not_1_out, not_2_out, not_3_out, not_4_out, not_5_out, not_6_out, not_7_out, not_8_out, not_9_out,
       not_10_out, not_11_out, not_12_out, not_13_out, not_14_out, not_15_out, not_16_out, not_17_out,
       not_18_out, not_19_out, not_20_out, not_21_out, not_22_out, not_23_out, not_24_out, not_25_out,
       not_26_out, not_27_out, not_28_out, not_29_out, not_30_out, not_31_out, not_32_out, not_33_out,
       not_34_out, not_35_out, not_36_out, not_37_out, not_38_out, not_39_out, not_40_out;

  not not_1 (not_1_out, RS);
  not not_2 (not_2_out, A);
  not not_3 (not_3_out, B);
  not not_4 (not_4_out, C);
  not not_5 (not_5_out, RS);
  not not_6 (not_6_out, B);
  not not_7 (not_7_out, RS);
  not not_8 (not_8_out, A);
  not not_9 (not_9_out, RS);
  not not_10 (not_10_out, D);
  not not_11 (not_11_out, RS);
  not not_12 (not_12_out, A);
  not not_13 (not_13_out, D);
  not not_14 (not_14_out, RS);
  not not_15 (not_15_out, A);
  not not_16 (not_16_out, RS);
  not not_17 (not_17_out, RS);
  not not_18 (not_18_out, A);
  not not_19 (not_19_out, B);
  not not_20 (not_20_out, C);
  not not_21 (not_21_out, RS);
  not not_22 (not_22_out, A);
  not not_23 (not_23_out, C);
  not not_24 (not_24_out, D);
  not not_25 (not_25_out, RS);
  not not_26 (not_26_out, A);
  not not_27 (not_27_out, RS);
  not not_28 (not_28_out, C);
  not not_29 (not_29_out, RS);
  not not_30 (not_30_out, B);
  not not_31 (not_31_out, D);
  not not_32 (not_32_out, RS);
  not not_33 (not_33_out, A);
  not not_34 (not_34_out, RS);
  not not_35 (not_35_out, RS);
  not not_36 (not_36_out, A);
  not not_37 (not_37_out, RS);
  not not_38 (not_38_out, C);
  not not_39 (not_39_out, RS);
  not not_40 (not_40_out, C);
  and and_1 (and_1_out, RD, not_1_out, not_2_out, not_3_out, not_4_out);
  and and_2 (and_2_out, RD, not_5_out, not_6_out, D);
  and and_3 (and_3_out, RD, not_7_out, not_8_out, C, D);
  and and_4 (and_4_out, RD, not_9_out, A, B, not_10_out);
  and and_5 (and_5_out, RD, not_11_out, not_12_out, not_13_out);
  and and_6 (and_6_out, RD, not_14_out, not_15_out, C);
  and and_7 (and_7_out, RD, not_16_out, B, C);
  and and_8 (and_8_out, RD, not_17_out, not_18_out, not_19_out, not_20_out);
  and and_9 (and_9_out, RD, not_21_out, not_22_out, not_23_out, not_24_out);
  and and_10 (and_10_out, RD, not_25_out, not_26_out, B, C);
  and and_11 (and_11_out, RD, not_27_out, A, not_28_out, D);
  and and_12 (and_12_out, RD, not_29_out, A, not_30_out, C, not_31_out);
  and and_13 (and_13_out, RD, not_32_out, not_33_out, C, D);
  and and_14 (and_14_out, RD, not_34_out, B, D);
  and and_15 (and_15_out, RD, not_35_out, not_36_out, B, C);
  and and_16 (and_16_out, RD, not_37_out, A, not_38_out, D);
  and and_17 (and_17_out, RD, not_39_out, A, B, not_40_out);
  or or_1 (S3, and_1_out, and_2_out, and_3_out, and_4_out);
  or or_2 (S2, and_5_out, and_6_out, and_7_out);
  or or_3 (S1, and_8_out, and_9_out, and_10_out, and_11_out, and_12_out);
  or or_4 (S0, and_13_out, and_14_out, and_15_out, and_16_out, and_17_out);
endmodule

module Display (
  input  S3,
  input  S2,
  input  S1,
  input  S0,
  output a,
  output b,
  output c,
  output d,
  output e,
  output f,
  output g
);

  wire and_1_out, and_2_out, and_3_out, and_4_out, and_5_out, and_6_out, and_7_out, and_8_out, and_9_out,
       and_10_out, and_11_out, and_12_out, and_13_out, and_14_out, and_15_out, and_16_out, and_17_out,
       and_18_out, and_19_out, and_20_out, and_21_out, and_22_out, and_23_out, and_24_out, and_25_out,
       and_26_out, and_27_out, and_28_out, and_29_out, and_30_out, and_31_out, and_32_out, and_33_out,
       and_34_out, and_35_out, not_1_out, not_2_out, not_3_out, not_4_out, not_5_out, not_6_out, not_7_out,
       not_8_out, not_9_out, not_10_out, not_11_out, not_12_out, not_13_out, not_14_out, not_15_out,
       not_16_out, not_17_out, not_18_out, not_19_out, not_20_out, not_21_out, not_22_out, not_23_out,
       not_24_out, not_25_out, not_26_out, not_27_out, not_28_out, not_29_out, not_30_out, not_31_out,
       not_32_out, not_33_out, not_34_out, not_35_out, not_36_out, not_37_out, not_38_out, not_39_out,
       not_40_out, not_41_out, not_42_out, not_43_out;

  not not_1 (not_1_out, S2);
  and and_1 (and_1_out, not_1_out, not_2_out);
  not not_2 (not_2_out, S0);
  not not_3 (not_3_out, S3);
  and and_2 (and_2_out, not_3_out, S1);
  not not_4 (not_4_out, S3);
  and and_3 (and_3_out, not_4_out, S2, S0);
  and and_4 (and_4_out, S2, S1);
  and and_5 (and_5_out, S3, not_5_out, not_6_out);
  not not_5 (not_5_out, S2);
  not not_6 (not_6_out, S1);
  and and_6 (and_6_out, S3, not_7_out);
  not not_7 (not_7_out, S0);
  not not_8 (not_8_out, S3);
  and and_7 (and_7_out, not_8_out, not_9_out);
  not not_9 (not_9_out, S2);
  not not_10 (not_10_out, S3);
  and and_8 (and_8_out, not_10_out, not_11_out, not_12_out);
  not not_11 (not_11_out, S1);
  not not_12 (not_12_out, S0);
  not not_13 (not_13_out, S2);
  and and_9 (and_9_out, not_13_out, not_14_out);
  not not_14 (not_14_out, S0);
  not not_15 (not_15_out, S3);
  and and_10 (and_10_out, not_15_out, S1, S0);
  and and_11 (and_11_out, S3, not_16_out, S0);
  not not_16 (not_16_out, S1);
  not not_17 (not_17_out, S3);
  and and_12 (and_12_out, not_17_out, not_18_out);
  not not_18 (not_18_out, S1);
  not not_19 (not_19_out, S3);
  and and_13 (and_13_out, not_19_out, S0);
  not not_20 (not_20_out, S1);
  and and_14 (and_14_out, not_20_out, S0);
  not not_21 (not_21_out, S3);
  and and_15 (and_15_out, not_21_out, S2);
  and and_16 (and_16_out, S3, not_22_out);
  not not_22 (not_22_out, S2);
  not not_23 (not_23_out, S3);
  not not_24 (not_24_out, S2);
  and and_17 (and_17_out, not_23_out, not_24_out, not_25_out);
  not not_25 (not_25_out, S0);
  not not_26 (not_26_out, S2);
  and and_18 (and_18_out, not_26_out, S1, S0);
  and and_19 (and_19_out, S2, not_27_out, S0);
  not not_27 (not_27_out, S1);
  and and_20 (and_20_out, S2, S1, not_28_out);
  not not_28 (not_28_out, S0);
  and and_21 (and_21_out, S3, not_29_out);
  not not_29 (not_29_out, S1);
  not not_30 (not_30_out, S2);
  and and_22 (and_22_out, not_30_out, not_31_out);
  not not_31 (not_31_out, S0);
  and and_23 (and_23_out, S1, not_32_out);
  not not_32 (not_32_out, S0);
  and and_24 (and_24_out, S3, S1);
  and and_25 (and_25_out, S3, S2);
  not not_33 (not_33_out, S1);
  and and_26 (and_26_out, not_33_out, not_34_out);
  not not_34 (not_34_out, S0);
  not not_35 (not_35_out, S3);
  and and_27 (and_27_out, not_35_out, S2, not_36_out);
  not not_36 (not_36_out, S1);
  and and_28 (and_28_out, S2, not_37_out);
  not not_37 (not_37_out, S0);
  and and_29 (and_29_out, S3, not_38_out);
  not not_38 (not_38_out, S2);
  and and_30 (and_30_out, S3, S1);
  not not_39 (not_39_out, S2);
  and and_31 (and_31_out, not_39_out, S1);
  and and_32 (and_32_out, S1, not_40_out);
  not not_40 (not_40_out, S0);
  not not_41 (not_41_out, S3);
  and and_33 (and_33_out, not_41_out, S2, not_42_out);
  not not_42 (not_42_out, S1);
  and and_34 (and_34_out, S3, not_43_out);
  not not_43 (not_43_out, S2);
  and and_35 (and_35_out, S3, S0);
  or or_1 (b, and_7_out, and_8_out, and_9_out, and_10_out, and_11_out);
  or or_2 (c, and_12_out, and_13_out, and_14_out, and_15_out, and_16_out);
  or or_3 (d, and_17_out, and_18_out, and_19_out, and_20_out, and_21_out);
  or or_4 (e, and_22_out, and_23_out, and_24_out, and_25_out);
  or or_5 (f, and_26_out, and_27_out, and_28_out, and_29_out, and_30_out);
  or or_6 (g, and_31_out, and_32_out, and_33_out, and_34_out, and_35_out);
  or or_7 (a, and_1_out, and_2_out, and_3_out, and_4_out, and_5_out, and_6_out);
endmodule

module \Simulação  (
  input  A,
  input  B,
  input  C,
  input  D,
  input  Ready
);

  wire Codificador_s0, Codificador_s1, Codificador_s2, Codificador_s3, display_1_a, display_1_b, display_1_c,
       display_1_d, display_1_e, display_1_f, display_1_g, Reset_out;

  LED S2 (.in(Codificador_s2));
  LED S3 (.in(Codificador_s3));
  _7_Segment_Display u_7_segment_display_1 (
    .g(display_1_g), .f(display_1_f), .a(display_1_a), .b(display_1_b), .e(display_1_e), .d(display_1_d),
    .c(display_1_c));  // open: dp
  LED S0 (.in(Codificador_s0));
  LED S1 (.in(Codificador_s1));
  Button Reset (.out(Reset_out));
  Display display_1 (
    .S3(Codificador_s3), .S2(Codificador_s2), .S1(Codificador_s1), .a(display_1_a), .S0(Codificador_s0),
    .b(display_1_b), .c(display_1_c), .d(display_1_d), .e(display_1_e), .f(display_1_f), .g(display_1_g));
  Codificador__Exemplo Codificador (
    .RD(Ready), .RS(Reset_out), .A(A), .B(B), .C(C), .D(D), .S3(Codificador_s3), .S2(Codificador_s2),
    .S1(Codificador_s1), .S0(Codificador_s0));

  // Notes on the sheet:
  //   Circuitos Combinacionasis
  //   Sistema de Codificação de 4-bits
endmodule
